# Fritzing sketch Blink (saved by Fritzing 0.9.1b)
breadboards: 1

parts:
  LED1 = LED - 5mm [color="Red (633nm)" package="5 mm [THT]"]
  R1 = Resistor [tolerance=±5% resistance=330 package=THT]
  Part1 = Arduino Uno (Rev3)

nets (from the breadboard view):
  N1: LED1.anode, R1.Pin_0, Part1.GND
  N2: R1.Pin_1, Part1.D9_PWM
