# Fritzing sketch Dim (saved by Fritzing 0.9.1b)
breadboards: 1

parts:
  LED1 = RGB LED (com. cathode, rgb) [package="5 mm [THT]"]
  R1 = Resistor [tolerance=±5% resistance=330 package=THT]
  R2 = Resistor [tolerance=±5% resistance=330 package=THT]
  R3 = Resistor [tolerance=±5% resistance=330 package=THT]
  R4 = Photocell (LDR) [package=THT]
  R5 = Resistor [tolerance=±5% resistance=10k package=THT]
  Part1 = Arduino Uno (Rev3)

nets:
  N1: LED1.red_anode, R1.Pin_1, Part1.D9_PWM
  GND: LED1.common_cathode, R5.Pin_0, Part1.GND
  N2: LED1.green_anode, R3.Pin_0
  N3: LED1.blue_anode, R2.Pin_0
  N4: R2.Pin_1, Part1.D11_PWM/MOSI
  N5: R3.Pin_1, Part1.D10_PWM/SS
  5V: R4.pin_0, Part1.5V
  N6: R4.pin_1, R5.Pin_1, Part1.A0
