# Fritzing sketch Jeopardy (saved by Fritzing 0.9.1b)
breadboards: 1

parts:
  LED1 = LED - 5mm [color="Red (633nm)" package="5 mm [THT]"]
  R1 = Resistor [tolerance=±5% resistance=330 package=THT]
  Part1 = Arduino Uno (Rev3)
  S1 = Pushbutton [package="[THT]"]
  LED2 = smd LED [color="Blue (470nm)" package="0805 [SMD]"]
  R2 = Resistor [tolerance=±5% resistance=330 package=THT]
  S2 = Pushbutton [package="[THT]"]
  R3 = Resistor [tolerance=±5% resistance=10k package=THT]
  R4 = Resistor [tolerance=±5% resistance=10k package=THT]

nets:
  GND: LED1.cathode, Part1.GND, LED2.cathode, R3.Pin_0, R4.Pin_0
  N1: LED1.anode, R1.Pin_0
  N2: R1.Pin_1, Part1.D10_PWM/SS
  N3: Part1.D8, S1.Pin_3, S1.Pin_4, R4.Pin_1
  N4: Part1.D9_PWM, S2.Pin_3, S2.Pin_4, R3.Pin_1
  N5: Part1.D11_PWM/MOSI, R2.Pin_1
  5V: Part1.5V, S1.Pin_1, S2.Pin_1, S2.Pin_2
  N6: LED2.anode, R2.Pin_0
