# Fritzing sketch Keyboard (saved by Fritzing 0.9.1b)
breadboards: 1

parts:
  LED1 = LED - 5mm [color="Red (633nm)" package="5 mm [THT]"]
  R1 = Resistor [tolerance=±5% resistance=330 package=THT]
  Part1 = Arduino Uno (Rev3)
  LED2 = smd LED [color="Blue (470nm)" package="0805 [SMD]"]
  R2 = Resistor [tolerance=±5% resistance=330 package=THT]
  S2 = Pushbutton [package="[THT]"]
  R3 = Resistor [tolerance=±5% resistance=10k package=THT]
  R4 = Resistor [tolerance=±5% resistance=10k package=THT]
  LED3 = smd LED [color="Yellow (595nm)" package="0805 [SMD]"]
  R5 = Resistor [tolerance=±5% resistance=330 package=THT]
  S3 = Pushbutton [package="[THT]"]
  R6 = Resistor [tolerance=±5% resistance=10k package=THT]
  R7 = Resistor [tolerance=±5% resistance=100 package=THT]
  J1 = Piezo Speaker
  S1 = Pushbutton [package="[THT]"]

nets (from the breadboard view):
  N1: LED1.cathode, Part1.GND, LED2.cathode, R3.Pin_0, R4.Pin_0, R6.Pin_0, J1.pin2
  N2: LED1.anode, R1.Pin_0
  N3: R1.Pin_1, Part1.D6_PWM
  N4: Part1.D8, R5.Pin_1
  N5: Part1.D9_PWM, R7.Pin_1
  N6: Part1.D10_PWM/SS, R4.Pin_1, S1.Pin_3, S1.Pin_4
  N7: Part1.D11_PWM/MOSI, S2.Pin_3, S2.Pin_4, R3.Pin_1
  N8: Part1.D12/MISO, S3.Pin_3, S3.Pin_4, R6.Pin_1
  N9: Part1.D7, R2.Pin_1
  N10: Part1.5V, S2.Pin_1, LED3.cathode, S3.Pin_1, S3.Pin_2, S1.Pin_1
  N11: LED2.anode, R2.Pin_0
  N12: LED3.anode, R5.Pin_0
  N13: R7.Pin_0, J1.pin1
