# Fritzing sketch MotionDetector (saved by Fritzing 0.9.1b)
breadboards: 1

parts:
  Part1 = Arduino Uno (Rev3)
  J1 = Piezo Speaker
  R6 = Resistor [tolerance=±5% resistance=10k package=THT]
  R7 = Rotary Potentiometer (Small) [maximum_resistance=10kΩ package=THT]

nets (from the breadboard view):
  N1: Part1.A0, R7.wiper
  N2: Part1.D9_PWM, R6.Pin_0
  N3: Part1.5V, R7.leg1
  N4: Part1.GND, J1.pin2, R7.leg2
  N5: J1.pin1, R6.Pin_1
