# Fritzing sketch Karaoke (saved by Fritzing 0.9.1b)
breadboards: 1

parts:
  Part3 = Arduino Uno (Rev3)
  R8 = Rotary Potentiometer (Small) [maximum_resistance=10kΩ package=THT]
  LCD2 = LCD screen
  J1 = Piezo Speaker
  R9 = Resistor [tolerance=±5% resistance=100 package=THT]
  S1 = Pushbutton [package="[THT]"]
  R10 = Resistor [tolerance=±5% resistance=10k package=THT]

nets:
  N1: Part3.D8, S1.Pin_1, S1.Pin_2, R10.Pin_0
  N2: Part3.D9_PWM, J1.pin2
  N3: Part3.D11_PWM/MOSI, LCD2.E
  N4: Part3.D12/MISO, LCD2.RS
  N5: Part3.D2, LCD2.LED-
  N6: Part3.D3_PWM, LCD2.LED+
  N7: Part3.D4, LCD2.DB7
  N8: Part3.D5_PWM, LCD2.DB6
  5V: Part3.5V, R8.leg2, LCD2.VDD, S1.Pin_3, S1.Pin_4
  GND: Part3.GND, R8.leg1, LCD2.VSS, LCD2.R/W, R9.Pin_1, R10.Pin_1
  N9: R8.wiper, LCD2.V0
  N10: J1.pin1, R9.Pin_0
