# Fritzing sketch Mood (saved by Fritzing 0.9.1b)
breadboards: 1

parts:
  Part1 = Arduino Uno (Rev3)
  R1 = Resistor [tolerance=±5% resistance=220 power=330 package=THT]
  R2 = Resistor [tolerance=±5% resistance=220 power=330 package=THT]
  R3 = Resistor [tolerance=±5% resistance=220 power=330 package=THT]
  T1 = LM35 Temperature Sensor [package="TO92 [THT]"]
  LED1 = RGB LED (com. cathode, rgb) [package="5 mm [THT]"]

nets:
  N1: Part1.A0, T1.Vout
  N2: Part1.D9_PWM, R3.Pin_0
  N3: Part1.D10_PWM/SS, R2.Pin_0
  N4: Part1.D11_PWM/MOSI, R1.Pin_0
  5V: Part1.5V, T1.+Vs
  GND: Part1.GND, T1.GND, LED1.common_cathode
  N5: R1.Pin_1, LED1.blue_anode
  N6: R2.Pin_1, LED1.green_anode
  N7: R3.Pin_1, LED1.red_anode

custom parts:
  RGB LED (com. cathode, rgb): A 5mm tri-color LED with red, green and blue inside.
