# Fritzing sketch Robot (saved by Fritzing 0.9.1b)
breadboards: 1

parts:
  Part3 = Arduino Uno (Rev3)
  S2 = Pushbutton [package="[THT]"]
  R9 = Resistor [tolerance=±5% resistance=10k package=THT]
  J2 = Basic Servo

nets:
  N1: Part3.D10_PWM/SS, J2.pulse
  GND: Part3.GND, R9.Pin_1, J2.gnd
  N2: Part3.D7, S2.Pin_1, S2.Pin_2, R9.Pin_0
  5V: Part3.5V, S2.Pin_4, J2.vcc
