# Fritzing sketch Spinner (saved by Fritzing 0.9.1b)
breadboards: 1

parts:
  Part3 = Arduino Uno (Rev3)
  S2 = Pushbutton [package="[THT]"]
  R13 = Resistor [tolerance=±5% resistance=10k package=THT]
  R14 = Resistor [tolerance=±5% resistance=330 package=THT]
  Q2 = NPN-Transistor [package="TO92 [THT]"]
  M2 = DC Motor
  D2 = Rectifier Diode [part_number=1N4001 package="300 mil [THT]"]

nets:
  N1: Part3.D9_PWM, R14.Pin_0
  N2: Part3.D11_PWM/MOSI, S2.Pin_1, S2.Pin_2, R13.Pin_1
  GND: Part3.GND, R13.Pin_0, Q2.C
  5V: Part3.5V, S2.Pin_3, S2.Pin_4, M2.pin_1, D2.cathode
  N3: R14.Pin_1, Q2.B
  N4: Q2.E, M2.pin_2, D2.anode
